# Fritzing sketch Main (saved by Fritzing 0.9.4)

parts:
  Компонент1 = Arduino Nano (Rev3.0)
  RS485_module1 = RS485 Module (MAX3485)
  M1 = RioRand LM2596
  Power_plug1 = Power plug
  Компонент2 = FC-28 Soil Hygrometer Module - Probe
  R2 = Resistor [tolerance=±5% resistance=4.7k package=THT]
  S1 = Pushbutton [package=THT]
  C1 = Ceramic Capacitor [capacitance=100nF package="100 mil [THT, multilayer]"]
  R3 = Resistor [tolerance=±5% resistance=10k package=THT]
  OLED_I2C1 = OLED 128x64 I2C Monochrome Display
  DS1 = DS18B20 1-Wire Temperature Sensor [part_number=DS18B20]
  R4 = Resistor [tolerance=±5% resistance=4.7k package=THT]
  S2 = Pushbutton [package=THT]

nets (from the breadboard view):
  GND: Компонент1.GND, RS485_module1.GND, M1.Pin_4, S1.leg0, C1.1, OLED_I2C1.GND, DS1.GND, S2.leg0
  N1: Компонент1.D3, C1.0, R3.Pin_1
  N2: Компонент1.D4, RS485_module1.RE, RS485_module1.DE
  N3: Компонент1.D8, RS485_module1.RO
  N4: Компонент1.D9, RS485_module1.DI
  N5: Компонент1.D10, R2.Pin_0
  N6: Компонент1.D11/MOSI, Компонент2.NEG
  N7: Компонент1.D12/MISO, DS1.DQ, R4.Pin_0
  N8: Компонент1.VIN, M1.Pin_3
  VDD: Компонент1.5V, RS485_module1.VCC, OLED_I2C1.VDD, DS1.VDD, R4.Pin_1
  N9: Компонент1.A5, OLED_I2C1.SCK
  N10: Компонент1.A4, OLED_I2C1.SDA
  N11: Компонент1.A0, Компонент2.POS, R2.Pin_1
  N12: Компонент1.D13/SCK, S2.leg1
  N13: M1.Pin_1, Power_plug1.VCC
  N14: M1.Pin_2, Power_plug1.GND
  N15: S1.leg1, R3.Pin_0

notes:
  DC-DC
  Щуп для измерения
  RS 485
  Кнопка для внесения каллибровки мин. показания и макс. показания
  Дисплей для показа тек. показания и режимов калибровки
  DS18B20 для определения температуры почвы
  перемычка (дефолтный адрес)

custom parts:
  RS485 Module (MAX3485): Commercially available RS485 to RS232 TTL Module
  FC-28 Soil Hygrometer Module - Probe: The FC-28 is a soil hygrometer module that uses the Texas Instruments LM393 comparator chip to provide an analog measurement of soil humidity.
